# Fritzing sketch NightLife-4LED (saved by Fritzing 0.8.7b)
circuit board: 5.94346cm x 1.678cm
breadboards: 1

parts:
  R1 = Photocell (LDR) [package=THT]
  R2 = Trimmer Potentiometer [maximum_resistance=10kΩ package=THT]
  R4 = Resistor [tolerance=±5% resistance=220 package=THT]
  Q2 = NPN-Transistor [package="TO92 [THT]"]
  R5 = Resistor [tolerance=±5% resistance=220 package=THT]
  C1 = Ceramic Capacitor [capacitance=100nF package="100 mil [THT, multilayer]"]
  Q3 = NPN-Transistor [package="TO92 [THT]"]
  L1 = Inductor [package="400 mil [THT]"]
  LED1 = LED - 5mm [color="Red (633nm)" package="5 mm [THT]"]
  LED2 = LED - 5mm [color="Red (633nm)" package="5 mm [THT]"]
  Q1 = NPN-Transistor [package="TO92 [THT]"]
  LED3 = LED - 5mm [color="Red (633nm)" package="5 mm [THT]"]
  LED4 = LED - 5mm [color="Red (633nm)" package="5 mm [THT]"]
  R3 = Resistor [tolerance=±5% resistance=220 package=THT]
  VCC1 = Battery

nets:
  N1: R1.pin_0, R2.leg2, Q1.B
  N2: R1.pin_1, L1.pin_0, Q1.C, VCC1.-
  N3: R2.leg1, R2.wiper, R3.Pin_1
  N4: R4.Pin_0, Q1.E
  N5: R4.Pin_1, Q2.C, R5.Pin_1, Q3.B
  N6: Q2.E, Q3.E, LED2.cathode, LED4.cathode, R3.Pin_0, VCC1.+
  N7: Q2.B, R5.Pin_0, C1.1
  N8: C1.0, Q3.C, L1.pin_1, LED1.anode, LED3.anode
  N9: LED1.cathode, LED2.anode
  N10: LED3.cathode, LED4.anode

notes:
  NightLife 4LED v0.1
  +
  -
